# Fritzing sketch Foot_Sensor (saved by Fritzing 0.9.5d)
breadboards: 1

parts:
  Part1 = Arduino Nano (Rev3.0)
  J1 = Basic Force Sensing Resistor (FSR) [package=THT]
  J2 = Basic Force Sensing Resistor (FSR) [package=THT]
  BAT1 = 18650 battery holder [package=battery-18650-kit]
  R1 = Resistor [tolerance=±5% resistance=220 package="0402 [SMD]"]
  R2 = Resistor [tolerance=±5% resistance=220 package="0402 [SMD]"]

nets:
  N1: Part1.GND, BAT1.-, R1.Pin_0, R2.Pin_0
  N2: Part1.VIN, J2.pin_1, BAT1.+
  N3: Part1.A0, J1.pin_1, R1.Pin_1
  N4: Part1.3V3, J1.pin_0, J2.pin_0

custom parts:
  18650 battery holder: 18650 Battery Holder
